// Logisim project BasicComputer.circ as structural Verilog: 3 circuits, main circuit main
module main (
  output [15:0] out_1,
  output out_2
);

  wire clock_1_out, INC_PC, LD_AC, LD_AR, LD_DR, LD_IR, LD_PC, MRead, Write;
  wire [2:0] ALU, BUS, Bus_t;
  wire [11:0] AR_q, bit_extender_1_out, bit_extender_2_out, PC_q;
  wire [15:0] AC, alu_1_ac_output, bit_extender_3_out, bit_extender_4_out, DR_q, IR, multiplexer_1_out, TR_q;

  Control_Unit control_unit_1 (
    .AC(AC), .IR(IR), .Clock(clock_1_out), .LD_DR(LD_DR), .write(Write), .Memory_Read(MRead), .LD_AC(LD_AC),
    .ALU(ALU), .LD_AR(LD_AR), .LD_PC(LD_PC), .LD_IR(LD_IR), .INC_PC(INC_PC), .BUS(Bus_t));
  Bit_Extender #(.in_width(16), .out_width(12)) bit_extender_1 (.in(multiplexer_1_out), .out(bit_extender_1_out));
  Bit_Extender #(.in_width(16), .out_width(12)) bit_extender_2 (.in(multiplexer_1_out), .out(bit_extender_2_out));
  Register #(.width(12)) AR (.D(bit_extender_1_out), .en(LD_AR), .Q(AR_q), .clk(clock_1_out));  // open: clr
  Register #(.width(16)) TR (.D(multiplexer_1_out), .Q(TR_q), .clk(clock_1_out));  // open: en, clr
  Register #(.width(16)) DR (.D(multiplexer_1_out), .en(LD_DR), .Q(DR_q), .clk(clock_1_out));  // open: clr
  Register #(.width(16)) u_AC (.D(alu_1_ac_output), .en(LD_AC), .Q(AC), .clk(clock_1_out));  // open: clr
  Counter #(.width(12), .max('hfff)) PC (
    .load(LD_PC), .D(bit_extender_2_out), .count(INC_PC), .Q(PC_q), .clk(clock_1_out));  // open: carry, clr
  Clock clock_1 (.out(clock_1_out));
  Register #(.width(16)) u_IR (.D(multiplexer_1_out), .en(LD_IR), .Q(IR), .clk(clock_1_out));  // open: clr
  RAM #(.addrWidth(12), .dataWidth(16), .bus("separate")) ram_1 (
    .addr(AR_q), .din(multiplexer_1_out), .data(out_1), .str(Write), .clk(clock_1_out), .ld(MRead));  // open: sel, clr
  assign bit_extender_3_out = {{4{1'b0}}, AR_q};  // Bit_Extender bit_extender_3
  assign bit_extender_4_out = {{4{1'b0}}, PC_q};  // Bit_Extender bit_extender_4
  ALU alu_1 (.A(DR_q), .B(AC), .Mux_Selector(ALU), .AC_output(alu_1_ac_output), .E(out_2));
  Multiplexer #(.select(3), .width(16)) multiplexer_1 (
    .in0(out_1), .in1(bit_extender_3_out), .in2(TR_q), .in3(DR_q), .in4(AC), .in5(bit_extender_4_out),
    .in6(IR), .out(multiplexer_1_out), .sel(BUS), .en(1'b1));  // open: in7
endmodule

module ALU (
  input  [15:0] A,
  input  [15:0] B,
  input  [2:0] Mux_Selector,
  output [15:0] AC_output,
  output E
);

  wire adder_1_cout;
  wire [15:0] adder_1_out, adder_2_out, and_1_out, bit_extender_1_out, or_1_out, subtractor_1_out, xor_1_out;

  assign bit_extender_1_out = {{15{1'b0}}, 1'b0};  // Bit_Extender bit_extender_1
  Adder #(.width(16)) adder_1 (.a(A), .b({16{1'b0}}), .out(adder_1_out), .cin(1'b1), .cout(adder_1_cout));
  assign and_1_out = A & B;  // AND_Gate and_1, 16 bits wide
  assign or_1_out = A | B;  // OR_Gate or_1, 16 bits wide
  assign xor_1_out = A ^ B;  // XOR_Gate xor_1, 16 bits wide
  Adder #(.width(16)) adder_2 (.a(A), .b(B), .out(adder_2_out), .cin(1'b0), .cout(adder_1_cout));
  Subtractor #(.width(16)) subtractor_1 (.a(A), .b(B), .out(subtractor_1_out), .bin(1'b0), .bout(adder_1_cout));
  Multiplexer #(.select(3), .width(16)) multiplexer_1 (
    .in1(adder_2_out), .in2(subtractor_1_out), .in3(A), .in4(and_1_out), .in5(or_1_out), .in6(xor_1_out),
    .in7(adder_1_out), .out(AC_output), .sel(Mux_Selector), .en(1'b1));  // open: in0
  or or_2 (E, adder_1_cout, adder_1_cout, adder_1_cout);
endmodule

module Control_Unit (
  input  [15:0] AC,
  input  [15:0] IR,
  input  Clock,
  output LD_DR,
  output write,
  output Memory_Read,
  output LD_AC,
  output [2:0] ALU,
  output LD_AR,
  output LD_PC,
  output LD_IR,
  output INC_PC,
  output [2:0] BUS
);

  wire AC_0, and_15_out, and_17_out, and_18_out, and_19_out, and_20_out, CLR_SC, D0, D0_D1_D2, D0_D1_D2_D5,
       D0_D1_D2_D5_T4, D0_D1_D2_D5_T5, D1, D2, D3, D3T4, D4, D5, D5T5, D5T6, D6, D7, D7B2, D7B2T3, D7B5,
       D7B5T3, D7B5T4, D7T3, D7T3B2_AC_0, d_ff_1_q, not_1_out, or_3_out, or_5_out, or_11_out, or_12_out,
       or_13_out, T0, T0___T2, T2, T3, T4, T4_D3_D4, T5, T6, T7;
  wire [2:0] SC_q;

  or or_1 (D0_D1_D2, D0, D1, D2);
  or or_2 (D0_D1_D2_D5, D0_D1_D2, D5);
  Decoder #(.select(3), .enable("false")) decoder_1 (
    .out0(D0), .out1(D1), .out2(D2), .out3(D3), .out4(D4), .out5(D5), .out6(D6), .out7(D7), .sel(IR[14:12]));
  not not_1 (not_1_out, CLR_SC);
  Counter #(.width(3), .max('h7)) SC (
    .count(not_1_out), .Q(SC_q), .clk(Clock), .clr(d_ff_1_q));  // open: load, D, carry
  D_Flip_Flop d_ff_1 (.clk(Clock), .D(CLR_SC), .Q(d_ff_1_q));  // open: Qn, preset, en, reset
  Decoder #(.select(3), .enable("false")) decoder_2 (
    .out0(T0), .out1(LD_IR), .out2(T2), .out3(T3), .out4(T4), .out5(T5), .out6(T6), .out7(T7), .sel(SC_q));
  or or_3 (or_3_out, AC[0], AC[1], AC[2], AC[3], AC[4], AC[5], AC[6], AC[7], AC[9], AC[10], AC[11], AC[12], AC[13], AC[14], AC[15], AC[8]);
  and and_1 (D7B5, D7, IR[5]);
  and and_2 (D7T3, D7, T3);
  and and_3 (D7B2, D7, IR[2]);
  and and_4 (D7T3B2_AC_0, D7B2, AC_0, T3);
  not not_2 (AC_0, or_3_out);
  and and_5 (D0_D1_D2_D5_T5, T5, D0_D1_D2_D5);
  and and_6 (D0_D1_D2_D5_T4, D0_D1_D2_D5, T4);
  and and_7 (write, D3, T4);
  and and_8 (D5T5, T5, D5);
  and and_9 (D5T6, D5, T6);
  or or_4 (T0___T2, T0, T2);
  and and_10 (LD_PC, D4, T4);
  and and_11 (D3T4, D3, T4);
  or or_5 (or_5_out, D4, D3);
  and and_12 (D7B5T4, T4, D7B5);
  and and_13 (D7B5T3, D7B5, T3);
  and and_14 (T4_D3_D4, T4, or_5_out);
  and and_15 (and_15_out, D0_D1_D2, T5);
  and and_16 (D7B2T3, D7B2, T3);
  or or_6 (LD_DR, D0_D1_D2_D5_T4, D5T5, D7B5T3);
  or or_7 (LD_AC, D0_D1_D2_D5_T5, D7B5T4, D5T6);
  or or_8 (LD_AR, T0, T2);
  or or_9 (INC_PC, D7T3B2_AC_0, LD_IR);
  and and_17 (and_17_out, D5, T5);
  or or_10 (CLR_SC, and_15_out, T4_D3_D4, D7B5T4, D5T6, D7B2T3);
  or or_11 (or_11_out, and_17_out, D5T5);
  or or_12 (or_12_out, D7B5T3, D3T4, D5T5);
  and and_18 (and_18_out, D2, T5);
  or or_13 (or_13_out, and_18_out, D5T5);
  or or_14 (Memory_Read, D0_D1_D2_D5_T4, LD_IR);
  and and_19 (and_19_out, D1, T5);
  and and_20 (and_20_out, D0, T5);
  Priority_Encoder priority_encoder_1 (
    .in0(Memory_Read), .in1(LD_PC), .in2(1'b0), .in3(1'b0), .in4(or_12_out), .in5(T0), .in6(T2), .in7(1'b0),
    .out(BUS));  // open: en_in, gs, en_out
  Priority_Encoder priority_encoder_2 (
    .in0(1'b0), .in1(and_19_out), .in2(D5T6), .in3(or_13_out), .in4(and_20_out), .in5(1'b0), .in6(1'b0),
    .in7(D7B5T4), .out(ALU));  // open: en_in, gs, en_out

  // Other names for the same wires on the sheet: M67 = AC[8]; D4T4 = LD_PC; B2 = IR[2]; B5 = IR[5]; I = IR[15];
  //   READ = Memory_Read; T1 = LD_IR
endmodule
